# Fritzing sketch Aufbau (saved by Fritzing 0.9.3b)
breadboards: 1

parts:
  Bauteil1 = Arduino Mega 2560 (Rev3)
  S1 = Round Pushbutton
  S2 = Round Pushbutton
  S3 = Round Pushbutton
  S4 = Round Pushbutton
  S5 = Round Pushbutton
  S6 = Round Pushbutton
  LED1 = LED - 3mm [color="Red (633nm)" package="3 mm [THT]"]
  LED2 = LED - 3mm [color="Red (633nm)" package="3 mm [THT]"]
  LED3 = LED - 3mm [color="Red (633nm)" package="3 mm [THT]"]
  LED4 = LED - 3mm [color="Red (633nm)" package="3 mm [THT]"]
  LED5 = LED - 3mm [color="Red (633nm)" package="3 mm [THT]"]
  LED6 = LED - 3mm [color="Red (633nm)" package="3 mm [THT]"]
  ULN1 = Darlington Driver [package=dil18]
  R1 = Resistor [tolerance=±5% resistance=10k package=THT]  # not connected
  R2 = Resistor [tolerance=±5% resistance=10k package=THT]

nets:
  N1: Bauteil1.D20/SDA, R2.Pin_0
  N2: Bauteil1.5V, LED1.anode, LED2.anode, LED3.anode, LED4.anode, LED5.anode, LED6.anode, ULN1.10, R2.Pin_1
  N3: Bauteil1.GND, S1.leg1, S2.leg1, S3.leg1, S4.leg1, S5.leg1, S6.leg1, ULN1.9
  N4: Bauteil1.D0_RX0, ULN1.8
  N5: Bauteil1.D1_TX0, ULN1.7
  N6: Bauteil1.D2_PWM, ULN1.6
  N7: Bauteil1.D3_PWM, ULN1.5
  N8: Bauteil1.D4_PWM, ULN1.4
  N9: Bauteil1.D5_PWM, ULN1.3
  N10: LED1.cathode, ULN1.15
  N11: LED2.cathode, ULN1.16
  N12: LED3.cathode, ULN1.14
  N13: LED4.cathode, ULN1.13
  N14: LED5.cathode, ULN1.12
  N15: LED6.cathode, ULN1.11
